# Fritzing sketch wiring (saved by Fritzing 0.9.3b)

parts:
  S3 = SWITCH-MOMENTARY-2 [package=reed_switch_pth]
  Windrichtungsanzeige = SWITCH-MOMENTARY-2 [package=reed_switch_pth]
  S5 = SWITCH-MOMENTARY-2 [package=reed_switch_pth]
  S6 = SWITCH-MOMENTARY-2 [package=reed_switch_pth]
  S7 = SWITCH-MOMENTARY-2 [package=reed_switch_pth]
  S8 = SWITCH-MOMENTARY-2 [package=reed_switch_pth]
  S9 = SWITCH-MOMENTARY-2 [package=reed_switch_pth]
  S10 = SWITCH-MOMENTARY-2 [package=reed_switch_pth]
  Regenmengenmesser = SWITCH-MOMENTARY-2 [package=reed_switch_pth]
  Bauteil1 = Arduino Pro Mini (3.3V)
  BME280 = BME280 Breakout
  BH1750 = BH1750
  Config-Taster = Momentary Switch [package=ksa_sealed_tac_switch]
  LED1 = LED - 3mm [color="Green (560nm)" package="3 mm [THT]"]
  Anemometer = SWITCH-MOMENTARY-2 [package=reed_switch_pth]
  R1 = Resistor [tolerance=±5% resistance=330 package=THT]
  R2 = Resistor [tolerance=±5% resistance=10k package=THT]
  R3 = Resistor [tolerance=±5% resistance=10k package=THT]
  R4 = Resistor [tolerance=±5% resistance=3.9k package=THT]
  R5 = Resistor [tolerance=±5% resistance=8.2k package=THT]
  R6 = Resistor [tolerance=±5% resistance=120k package=THT]
  R7 = Resistor [tolerance=±5% resistance=1k package=THT]
  R8 = Resistor [tolerance=±5% resistance=2.2k package=THT]
  R9 = Resistor [tolerance=±5% resistance=64.9k package=THT]
  R10 = Resistor [tolerance=±5% resistance=82k package=THT]
  R11 = Resistor [tolerance=±5% resistance=16k package=THT]
  C4 = Ceramic Capacitor [capacitance="100 nF" package="1206 [SMD, multilayer]"]
  C5 = Ceramic Capacitor [capacitance="100 nF" package="1206 [SMD, multilayer]"]
  Antenne_~8_3cm = CC1101 [part_number=CC1101]

nets:
  N1: S3.1, R6.Pin_0
  N2: Windrichtungsanzeige.1, R5.Pin_1
  GND: S5.1, Regenmengenmesser.1, Bauteil1.GND, BME280.GND, BH1750.GND, Config-Taster.4, LED1.cathode, R2.Pin_0, C4.1, Antenne_~8_3cm.2
  N3: S5.2, R7.Pin_1
  N4: S6.1, R4.Pin_0
  N5: S7.1, R10.Pin_0
  N6: S8.1, R8.Pin_1
  N7: S9.2, R9.Pin_0
  N8: S10.2, R11.Pin_1
  N9: Regenmengenmesser.2, Bauteil1.D6, R2.Pin_1, C4.0
  N10: Bauteil1.A4, BME280.SDI/SDA, BH1750.SDA
  N11: Bauteil1.A5, BME280.SCK/SCL, BH1750.SCL
  VCC: Bauteil1.VCC, BME280.3.3V, BH1750.VCC, Antenne_~8_3cm.1
  N12: Bauteil1.A2, R8.Pin_0
  N13: Bauteil1.SCK, Antenne_~8_3cm.4
  N14: Bauteil1.MISO, Antenne_~8_3cm.5
  N15: Bauteil1.MOSI, Antenne_~8_3cm.3
  N16: Bauteil1.D10, Antenne_~8_3cm.8
  N17: Bauteil1.D8, Config-Taster.3
  N18: Bauteil1.D5, R3.Pin_1, C5.0
  N19: Bauteil1.D4, R1.Pin_0
  N20: Bauteil1.D2, Antenne_~8_3cm.7
  N21: LED1.anode, R1.Pin_1
  N22: Anemometer.1, R3.Pin_0, C5.1
  N23: R4.Pin_1, R11.Pin_0

custom parts:
  BH1750: Light Sensor
